// Logisim project EE460_DA05_1935151.circ as structural Verilog: 4 circuits, main circuit Main
module Datapath (
  input  dec_i,
  input  init,
  input  [7:0] input_i,
  input  [7:0] dataIn,
  input  [7:0] input_x,
  input  [7:0] input_tr,
  input  inc_tr,
  output [7:0] frequency,
  output done,
  output [7:0] address,
  output a_x
);

  wire clk_out, comparator_1_eq, comparator_2_gt, not_2_out;
  wire [7:0] tr_q, x_q;

  Clock clk (.out(clk_out));
  Register x (.D(input_x), .en(init), .Q(x_q), .clk(clk_out));  // open: clr
  not not_1 (a_x, comparator_1_eq);
  Comparator comparator_1 (.a(dataIn), .b(x_q), .eq(comparator_1_eq));  // open: gt, lt
  Counter tr (.load(init), .D(input_tr), .count(inc_tr), .Q(tr_q), .up(1'b1), .clk(clk_out));  // open: carry, clr
  Counter #(.ongoal("stay")) i (
    .load(init), .D(input_i), .count(dec_i), .Q(address), .up(1'b0), .clk(clk_out));  // open: carry, clr
  not not_2 (not_2_out, comparator_2_gt);
  Comparator #(.mode("unsigned")) comparator_2 (.a(address), .b({8{1'b0}}), .gt(comparator_2_gt));  // open: eq, lt
  Register #(.width(1)) done_reg (.D(not_2_out), .Q(done), .clk(clk_out));  // open: en, clr
  Register freq (.D(tr_q), .en(not_2_out), .Q(frequency), .clk(clk_out));  // open: clr
endmodule

module CountNox (
  input  [7:0] DataOut,
  input  go,
  input  [7:0] x,
  output [7:0] freq,
  output done,
  output [7:0] address
);

  wire controlunit_1_dec_i, controlunit_1_inc_tr, controlunit_1_init, datapath_1_a_x;

  controlUnit controlunit_1 (
    .go(go), .done(done), .a_x(datapath_1_a_x), .dec_i(controlunit_1_dec_i), .inc_tr(controlunit_1_inc_tr),
    .init(controlunit_1_init));
  Datapath datapath_1 (
    .dec_i(controlunit_1_dec_i), .init(controlunit_1_init), .input_i({8{1'b1}}), .dataIn(DataOut),
    .input_x(x), .input_tr({8{1'b0}}), .inc_tr(controlunit_1_inc_tr), .frequency(freq), .done(done),
    .address(address), .a_x(datapath_1_a_x));
endmodule

module controlUnit (
  input  go,
  input  done,
  input  a_x,
  output dec_i,
  output inc_tr,
  output init
);

  wire clock_1_out, multiplexer_1_out;
  wire [2:0] multiplexer_2_out, register_1_q;
  wire [10:3] rom_1_data;

  Register #(.width(3)) register_1 (
    .D(multiplexer_2_out), .en(1'b1), .Q(register_1_q), .clk(clock_1_out));  // open: clr
  Clock clock_1 (.out(clock_1_out));
  ROM #(.addrWidth(3), .dataWidth(11)) rom_1 (.addr(register_1_q), .data({rom_1_data, init, inc_tr, dec_i}));
  Multiplexer #(.select(2)) multiplexer_1 (
    .in0(go), .in1(done), .in2(a_x), .in3(1'b1), .out(multiplexer_1_out), .sel(rom_1_data[10:9]));
  Multiplexer #(.width(3)) multiplexer_2 (
    .in0(rom_1_data[8:6]), .in1(rom_1_data[5:3]), .out(multiplexer_2_out), .sel(multiplexer_1_out));

  // Notes on the sheet:
  //   contents of rom_1 (hex, n*v repeats v):
  //   8 694 2c0 4a1 692
endmodule

module Main (
  input  go,
  input  [7:0] x,
  output [7:0] freq,
  output done
);

  wire [7:0] a_data, countnox_1_address;

  ROM a (.addr(countnox_1_address), .data(a_data));
  Clock clock_1 ();  // open: out
  CountNox countnox_1 (.DataOut(a_data), .go(go), .x(x), .freq(freq), .done(done), .address(countnox_1_address));

  // Notes on the sheet:
  //   contents of a (hex, n*v repeats v):
  //   35*0 1 6*0 1 16*0 1
endmodule
